// Logisim project RISC V.circ as structural Verilog: 1 circuit, main circuit main
module main (
  input  [3:0] in_1,
  input  Clock,
  input  in_3
);

  wire and_1_out, and_2_out, and_3_out, and_4_out, and_5_out, and_6_out, and_7_out, and_8_out, and_9_out,
       and_10_out, and_11_out, and_12_out, and_13_out, and_14_out, and_15_out, and_16_out, and_17_out,
       and_18_out, and_19_out, and_20_out, and_21_out, and_22_out, and_23_out, and_24_out, and_25_out,
       and_26_out, and_27_out, and_28_out, and_29_out, and_30_out, and_31_out, and_32_out, decoder_1_out0,
       decoder_1_out1, decoder_1_out2, decoder_1_out3, decoder_1_out4, decoder_1_out5, decoder_1_out6,
       decoder_1_out7, decoder_1_out8, decoder_1_out9, decoder_1_out10, decoder_1_out11, decoder_1_out12,
       decoder_1_out13, decoder_1_out14, decoder_1_out15, decoder_1_out16, decoder_1_out17, decoder_1_out18,
       decoder_1_out19, decoder_1_out20, decoder_1_out21, decoder_1_out22, decoder_1_out23, decoder_1_out24,
       decoder_1_out25, decoder_1_out26, decoder_1_out27, decoder_1_out28, decoder_1_out29, decoder_1_out30,
       decoder_1_out31;
  wire [2:0] rom_1_data_3;
  wire [3:0] adder_1_out, register_1_q;
  wire [4:0] rom_1_data_2;
  wire [31:0] adder_2_out, and_33_out, multiplexer_1_out, multiplexer_2_out, multiplexer_3_out,
       multiplexer_4_out, multiplexer_5_out, not_1_out, or_1_out, register_2_q, register_3_q, register_4_q,
       register_5_q, register_6_q, register_7_q, register_8_q, register_9_q, register_10_q, register_11_q,
       register_12_q, register_13_q, register_14_q, register_15_q, register_16_q, register_17_q,
       register_18_q, register_19_q, register_20_q, register_21_q, register_22_q, register_23_q,
       register_24_q, register_25_q, register_26_q, register_27_q, register_28_q, register_29_q,
       register_30_q, register_31_q, register_32_q, register_33_q, rom_1_data, shifter_2_out, shifter_3_out,
       xor_1_out;

  Register #(.width(4)) register_1 (.D(adder_1_out), .Q(register_1_q), .clk(Clock));  // open: en, clr
  Adder #(.width(4)) adder_1 (.a(in_1), .b(register_1_q), .out(adder_1_out));  // open: cin, cout
  ROM #(.addrWidth(4), .dataWidth(32)) rom_1 (
    .addr(register_1_q),
    .data({rom_1_data[31:24], rom_1_data_2[4], rom_1_data_2[0], rom_1_data_2[1], rom_1_data_2[2], rom_1_data[19:15], rom_1_data_3, rom_1_data[11:0]}));  // open: sel
  RAM ram_1 ();  // open: addr, data, sel, clk, ld, clr
  Decoder #(.select(5), .enable("false")) decoder_1 (
    .out0(decoder_1_out0), .out1(decoder_1_out1), .out2(decoder_1_out2), .out3(decoder_1_out3),
    .out4(decoder_1_out4), .out5(decoder_1_out5), .out6(decoder_1_out6), .out7(decoder_1_out7),
    .out8(decoder_1_out8), .out9(decoder_1_out9), .out10(decoder_1_out10), .out11(decoder_1_out11),
    .out12(decoder_1_out12), .out13(decoder_1_out13), .out14(decoder_1_out14), .out15(decoder_1_out15),
    .out16(decoder_1_out16), .out17(decoder_1_out17), .out18(decoder_1_out18), .out19(decoder_1_out19),
    .out20(decoder_1_out20), .out21(decoder_1_out21), .out22(decoder_1_out22), .out23(decoder_1_out23),
    .out24(decoder_1_out24), .out25(decoder_1_out25), .out26(decoder_1_out26), .out27(decoder_1_out27),
    .out28(decoder_1_out28), .out29(decoder_1_out29), .out30(decoder_1_out30), .out31(decoder_1_out31),
    .sel(rom_1_data[11:7]));
  and and_1 (and_1_out, decoder_1_out0, 1'b1);
  and and_2 (and_2_out, decoder_1_out1, 1'b1);
  and and_3 (and_3_out, decoder_1_out2, 1'b1);
  and and_4 (and_4_out, decoder_1_out3, 1'b1);
  and and_5 (and_5_out, decoder_1_out4, 1'b1);
  and and_6 (and_6_out, decoder_1_out5, 1'b1);
  and and_7 (and_7_out, decoder_1_out6, 1'b1);
  and and_8 (and_8_out, decoder_1_out7, 1'b1);
  and and_9 (and_9_out, decoder_1_out8, 1'b1);
  and and_10 (and_10_out, decoder_1_out9, 1'b1);
  and and_11 (and_11_out, decoder_1_out10, 1'b1);
  and and_12 (and_12_out, decoder_1_out11, 1'b1);
  and and_13 (and_13_out, decoder_1_out12, 1'b1);
  and and_14 (and_14_out, decoder_1_out13, 1'b1);
  and and_15 (and_15_out, decoder_1_out14, 1'b1);
  and and_16 (and_16_out, decoder_1_out15, 1'b1);
  Register #(.width(32)) register_2 (
    .D(multiplexer_5_out), .en(and_2_out), .Q(register_2_q), .clk(Clock));  // open: clr
  Register #(.width(32)) register_3 (
    .D(multiplexer_5_out), .en(and_3_out), .Q(register_3_q), .clk(Clock));  // open: clr
  Register #(.width(32)) register_4 (
    .D(multiplexer_5_out), .en(and_4_out), .Q(register_4_q), .clk(Clock));  // open: clr
  Register #(.width(32)) register_5 (
    .D(multiplexer_5_out), .en(and_5_out), .Q(register_5_q), .clk(Clock));  // open: clr
  Register #(.width(32)) register_6 (
    .D(multiplexer_5_out), .en(and_6_out), .Q(register_6_q), .clk(Clock));  // open: clr
  Register #(.width(32)) register_7 (
    .D(multiplexer_5_out), .en(and_7_out), .Q(register_7_q), .clk(Clock));  // open: clr
  Register #(.width(32)) register_8 (
    .D(multiplexer_5_out), .en(and_8_out), .Q(register_8_q), .clk(Clock));  // open: clr
  Register #(.width(32)) register_9 (
    .D(multiplexer_5_out), .en(and_9_out), .Q(register_9_q), .clk(Clock));  // open: clr
  Register #(.width(32)) register_10 (
    .D(multiplexer_5_out), .en(and_10_out), .Q(register_10_q), .clk(Clock));  // open: clr
  Register #(.width(32)) register_11 (
    .D(multiplexer_5_out), .en(and_11_out), .Q(register_11_q), .clk(Clock));  // open: clr
  Register #(.width(32)) register_12 (
    .D(multiplexer_5_out), .en(and_12_out), .Q(register_12_q), .clk(Clock));  // open: clr
  Register #(.width(32)) register_13 (
    .D(multiplexer_5_out), .en(and_13_out), .Q(register_13_q), .clk(Clock));  // open: clr
  Register #(.width(32)) register_14 (
    .D(multiplexer_5_out), .en(and_14_out), .Q(register_14_q), .clk(Clock));  // open: clr
  Register #(.width(32)) register_15 (
    .D(multiplexer_5_out), .en(and_15_out), .Q(register_15_q), .clk(Clock));  // open: clr
  Register #(.width(32)) register_16 (
    .D(multiplexer_5_out), .en(and_16_out), .Q(register_16_q), .clk(Clock));  // open: clr
  Register #(.width(32)) register_17 (.D({32{1'b0}}), .en(and_1_out), .Q(register_17_q), .clk(Clock));  // open: clr
  and and_17 (and_17_out, decoder_1_out16, 1'b1);
  and and_18 (and_18_out, decoder_1_out17, 1'b1);
  and and_19 (and_19_out, decoder_1_out18, 1'b1);
  and and_20 (and_20_out, decoder_1_out19, 1'b1);
  and and_21 (and_21_out, decoder_1_out20, 1'b1);
  and and_22 (and_22_out, decoder_1_out21, 1'b1);
  and and_23 (and_23_out, decoder_1_out22, 1'b1);
  and and_24 (and_24_out, decoder_1_out23, 1'b1);
  and and_25 (and_25_out, decoder_1_out24, 1'b1);
  and and_26 (and_26_out, decoder_1_out25, 1'b1);
  and and_27 (and_27_out, decoder_1_out26, 1'b1);
  and and_28 (and_28_out, decoder_1_out27, 1'b1);
  and and_29 (and_29_out, decoder_1_out28, 1'b1);
  and and_30 (and_30_out, decoder_1_out29, 1'b1);
  and and_31 (and_31_out, decoder_1_out30, 1'b1);
  and and_32 (and_32_out, decoder_1_out31, 1'b1);
  Register #(.width(32)) register_18 (
    .D(multiplexer_5_out), .en(and_17_out), .Q(register_18_q), .clk(Clock));  // open: clr
  Register #(.width(32)) register_19 (
    .D(multiplexer_5_out), .en(and_18_out), .Q(register_19_q), .clk(Clock));  // open: clr
  Register #(.width(32)) register_20 (
    .D(multiplexer_5_out), .en(and_19_out), .Q(register_20_q), .clk(Clock));  // open: clr
  Register #(.width(32)) register_21 (
    .D(multiplexer_5_out), .en(and_20_out), .Q(register_21_q), .clk(Clock));  // open: clr
  Register #(.width(32)) register_22 (
    .D(multiplexer_5_out), .en(and_21_out), .Q(register_22_q), .clk(Clock));  // open: clr
  Register #(.width(32)) register_23 (
    .D(multiplexer_5_out), .en(and_22_out), .Q(register_23_q), .clk(Clock));  // open: clr
  Register #(.width(32)) register_24 (
    .D(multiplexer_5_out), .en(and_23_out), .Q(register_24_q), .clk(Clock));  // open: clr
  Register #(.width(32)) register_25 (
    .D(multiplexer_5_out), .en(and_24_out), .Q(register_25_q), .clk(Clock));  // open: clr
  Register #(.width(32)) register_26 (
    .D(multiplexer_5_out), .en(and_25_out), .Q(register_26_q), .clk(Clock));  // open: clr
  Register #(.width(32)) register_27 (
    .D(multiplexer_5_out), .en(and_26_out), .Q(register_27_q), .clk(Clock));  // open: clr
  Register #(.width(32)) register_28 (
    .D(multiplexer_5_out), .en(and_27_out), .Q(register_28_q), .clk(Clock));  // open: clr
  Register #(.width(32)) register_29 (
    .D(multiplexer_5_out), .en(and_28_out), .Q(register_29_q), .clk(Clock));  // open: clr
  Register #(.width(32)) register_30 (
    .D(multiplexer_5_out), .en(and_29_out), .Q(register_30_q), .clk(Clock));  // open: clr
  Register #(.width(32)) register_31 (
    .D(multiplexer_5_out), .en(and_30_out), .Q(register_31_q), .clk(Clock));  // open: clr
  Register #(.width(32)) register_32 (
    .D(multiplexer_5_out), .en(and_31_out), .Q(register_32_q), .clk(Clock));  // open: clr
  Register #(.width(32)) register_33 (
    .D(multiplexer_5_out), .en(and_32_out), .Q(register_33_q), .clk(Clock));  // open: clr
  Multiplexer #(.select(5), .width(32), .enable("false")) multiplexer_1 (
    .in0(register_17_q), .in1(register_2_q), .in2(register_3_q), .in3(register_4_q), .in4(register_5_q),
    .in5(register_6_q), .in6(register_7_q), .in7(register_8_q), .in8(register_9_q), .in9(register_10_q),
    .in10(register_11_q), .in11(register_12_q), .in12(register_13_q), .in13(register_14_q),
    .in14(register_15_q), .in15(register_16_q), .in16(register_18_q), .in17(register_19_q),
    .in18(register_20_q), .in19(register_21_q), .in20(register_22_q), .in21(register_23_q),
    .in22(register_24_q), .in23(register_25_q), .in24(register_26_q), .in25(register_27_q),
    .in26(register_28_q), .in27(register_29_q), .in28(register_30_q), .in29(register_31_q),
    .in30(register_32_q), .in31(register_33_q), .out(multiplexer_1_out), .sel(rom_1_data[19:15]));
  Multiplexer #(.select(5), .width(32), .enable("false")) multiplexer_2 (
    .in0(register_17_q), .in1(register_2_q), .in2(register_3_q), .in3(register_4_q), .in4(register_5_q),
    .in5(register_6_q), .in6(register_7_q), .in7(register_8_q), .in8(register_9_q), .in9(register_10_q),
    .in10(register_11_q), .in11(register_12_q), .in12(register_13_q), .in13(register_14_q),
    .in14(register_15_q), .in15(register_16_q), .in16(register_18_q), .in17(register_19_q),
    .in18(register_20_q), .in19(register_21_q), .in20(register_22_q), .in21(register_23_q),
    .in22(register_24_q), .in23(register_25_q), .in24(register_26_q), .in25(register_27_q),
    .in26(register_28_q), .in27(register_29_q), .in28(register_30_q), .in29(register_31_q),
    .in30(register_32_q), .in31(register_33_q), .out(multiplexer_2_out),
    .sel({rom_1_data[24], rom_1_data_2[4], rom_1_data_2[0], rom_1_data_2[1], rom_1_data_2[2]}));
  Multiplexer #(.width(32), .enable("false")) multiplexer_3 (
    .in0({{20{in_3}}, rom_1_data[31:24], rom_1_data_2[4], rom_1_data_2[0], rom_1_data_2[1], rom_1_data_2[2]}),
    .in1(multiplexer_2_out), .out(multiplexer_3_out), .sel(rom_1_data[5]));
  assign not_1_out = ~multiplexer_3_out;  // NOT_Gate not_1, 32 bits wide
  Multiplexer #(.width(32), .enable("false")) multiplexer_4 (
    .in0(multiplexer_3_out), .in1(not_1_out), .out(multiplexer_4_out), .sel(rom_1_data[30]));
  assign and_33_out = multiplexer_1_out & multiplexer_3_out;  // AND_Gate and_33, 32 bits wide
  Shifter #(.width(32), .shift("ar")) shifter_1 (
    .in(multiplexer_1_out), .\dist ({{2{rom_1_data_2[4]}}, rom_1_data_2[2:0]}));  // open: out
  assign or_1_out = multiplexer_1_out | multiplexer_3_out;  // OR_Gate or_1, 32 bits wide
  assign xor_1_out = multiplexer_1_out ^ multiplexer_3_out;  // XOR_Gate xor_1, 32 bits wide
  Shifter #(.width(32), .shift("lr")) shifter_2 (
    .in(multiplexer_1_out), .\dist ({{2{rom_1_data_2[4]}}, rom_1_data_2[2:0]}), .out(shifter_2_out));
  Shifter #(.width(32)) shifter_3 (
    .in(multiplexer_1_out), .\dist ({{2{rom_1_data_2[4]}}, rom_1_data_2[2:0]}), .out(shifter_3_out));
  Adder #(.width(32)) adder_2 (
    .a(multiplexer_1_out), .b(multiplexer_4_out), .out(adder_2_out), .cin(rom_1_data[30]));  // open: cout
  Multiplexer #(.select(3), .width(32), .enable("false")) multiplexer_5 (
    .in0(adder_2_out), .in1(shifter_3_out), .in4(xor_1_out), .in5(shifter_2_out), .in6(or_1_out),
    .in7(and_33_out), .out(multiplexer_5_out), .sel(rom_1_data_3));  // open: in2, in3

  // Notes on the sheet:
  //   R-TYPE INCLUDES
  //   ADD,AND,OR,SUB,XOR
  //   I-TYPE INCLUDES
  //   ADDI,ANDI,ORI,XORI,SLLI,SRLI,SRAI
  //   TOTAL COMMANDS
  //   12 COMMANDS OF TWO TYPES
  //   Program Counter
  //   IMEM
  //   contents of rom_1 (hex, n*v repeats v):
  //   5002b3
  //   R-TYPE BITS GENERATOR
  //   mohammad umar 19b-136-cs(b)
  //   RISC V 
  //   FOR IMMEDIATE GENERATION
  //   5 BITS IMM
  //   FOR SLLI SRLI SRAI
  //   x1
  //   x4
  //   x5
  //   x11
  //   x13
  //   REGISTER FILE
  //   x2
  //   x3
  //   x6
  //   x7
  //   x8
  //   x9
  //   x10
  //   x12
  //   x14
  //   x15
  //   x0
  //   x16
  //   x17
  //   x18
  //   x19
  //   x20
  //   x21
  //   x22
  //   x23
  //   x24
  //   x25
  //   x26
  //   x27
  //   x28
  //   x29
  //   x30
  //   x31
  //   R AND I TYPE DIFFRENTIATOR
  //   Gives rs1 
  //   Gives rs2
  //   FUNC 3
  //   ALU BLOCK
  //   OR BLOCK
  //   XOR BLOCK
  //   left logical
  //   AND BLOCK
  //   Right logical
  //   ADDER/SUB BLOCK
endmodule
